# Fritzing sketch LM35 (saved by Fritzing 1.0.5)
breadboards: 1

parts:
  T1 = LM35 Temperature Sensor [package="TO92 [THT]"]
  Part1 = Arduino Uno (Rev3)

nets:
  N1: T1.+Vs, Part1.5V
  N2: T1.Vout, Part1.A0
  GND: T1.GND, Part1.GND
